# Fritzing sketch RFID card reader with Adafruit ESP32 Feather (saved by Fritzing 0.9.3b)
breadboards: 1

parts:
  Part1 = RFID USB Reader
  Part2 = Adafruit HUZZAH32 ESP32 Feather [part_number="Adafruit #3405"]
  R1 = Resistor [tolerance=±5% resistance=330 package=THT]
  LED1 = LED - 5mm [color="Green (555nm)" package="5 mm [THT]"]
  C1 = Electrolytic Capacitor [capacitance=0.47mF package="100 mil [THT, electrolytic]"]
  D1 = Rectifier Diode [part_number=1N4001 package="300 mil [THT]"]  # not connected

nets:
  N1: Part1.TX-O, Part2.IO16
  GND: Part1.GND, Part2.GND, R1.Pin_0, C1.-
  VCC: Part1.VCC, Part2.3.3V, C1.+
  N2: R1.Pin_1, LED1.cathode

notes:
  330 ohm
  470 uF
  GIO12 -GRN LED
  GIO16 - RXD (UART2)
  Adafruit ESP32 Feather
  Sparkfun RFID USB Reader
  RFID Reader ID-12LA (125 kHz)
